# Fritzing sketch AndroidProcessingControler(stripboard) (saved by Fritzing 0.7.12b)
breadboards: 1

parts:
  Arduino1 = Arduino
  S1 = Pushbutton [package="[THT]"]
  R1 = Resistor [tolerance=±5% resistance=10k package=THT]
  R2 = Rotary Potentiometer (Small) [maximum_resistance=100kΩ]

nets:
  N1: Arduino1.D2, S1.Pin_1, S1.Pin_2, R1.Pin_0
  N2: Arduino1.+5V, S1.Pin_3, S1.Pin_4, R2.leg2
  N3: Arduino1.GND, R1.Pin_1, R2.leg1
  N4: Arduino1.A0, R2.wiper
